# Fritzing sketch Tanks Mon Arduino  (saved by Fritzing 0.9.3b)
circuit board: 8.41874cm x 5.64444cm
breadboards: 1

parts:
  Part1 = Arduino Uno (Rev3)
  SR04T1 = JSN SR04T Sonar Controller [part_number=JSN-SR04T-2.0]
  SR04T2 = JSN SR04T Sonar Controller [part_number=JSN-SR04T-2.0]

nets:
  N1: Part1.D2, SR04T1.TX_Echo
  N2: Part1.D3_PWM, SR04T1.RX_Trig
  N3: Part1.D4, SR04T2.TX_Echo
  N4: Part1.D5_PWM, SR04T2.RX_Trig
  5V: Part1.5V, SR04T1.5V, SR04T2.5V
  GND: Part1.GND, SR04T1.Gnd, SR04T2.Gnd

custom parts:
  JSN SR04T Sonar Controller: Control board for sonar
